// Logisim project week06_shiftregister.circ as structural Verilog: 6 circuits, main circuit main
module main (
  input  SerialData,
  input  in_2,
  input  in_3
);

  wire clock_1_out, clock_2_out, shreg74hc595_1_q0, shreg74hc595_1_q1, shreg74hc595_1_q2, shreg74hc595_1_q3,
       shreg74hc595_1_q4, shreg74hc595_1_q5, shreg74hc595_1_q6, shreg74hc595_1_q7;

  _7_Segment_Display u_7_segment_display_1 (
    .g(shreg74hc595_1_q0), .f(shreg74hc595_1_q1), .a(shreg74hc595_1_q2), .b(shreg74hc595_1_q3),
    .e(shreg74hc595_1_q7), .d(shreg74hc595_1_q6), .c(shreg74hc595_1_q5), .dp(shreg74hc595_1_q4));
  ShReg74HC595 shreg74hc595_1 (
    .Q3(shreg74hc595_1_q3), .Q1(shreg74hc595_1_q1), .STCP(clock_1_out), .SHCP(clock_2_out),
    .Q5(shreg74hc595_1_q5), .DS(SerialData), .MR(in_3), .OE(in_2), .Q0(shreg74hc595_1_q0),
    .Q2(shreg74hc595_1_q2), .Q4(shreg74hc595_1_q4), .Q6(shreg74hc595_1_q6), .Q7(shreg74hc595_1_q7));  // open: Q7s
  Clock #(.lowDuration(63)) clock_1 (.out(clock_1_out));
  Clock #(.highDuration(2), .lowDuration(6)) clock_2 (.out(clock_2_out));
  Clock sysclk ();  // open: out
endmodule

module ShReg74HC595 (
  input  DS,
  input  SHCP,
  input  MR,
  input  STCP,
  input  OE,
  output Q7s,
  output Q0,
  output Q1,
  output Q2,
  output Q3,
  output Q4,
  output Q5,
  output Q6,
  output Q7
);

  wire d_ff_1_q, d_ff_2_q, d_ff_3_q, d_ff_4_q, d_ff_5_q, d_ff_6_q, d_ff_7_q, d_ff_8_q, d_ff_9_q, d_ff_10_q,
       d_ff_11_q, d_ff_12_q, d_ff_13_q, d_ff_14_q, d_ff_16_q, not_1_out, not_2_out;

  D_Flip_Flop d_ff_1 (.D(DS), .clk(SHCP), .Q(d_ff_1_q), .reset(not_1_out));  // open: Qn, preset
  not not_1 (not_1_out, MR);
  not not_2 (not_2_out, OE);
  D_Flip_Flop d_ff_2 (.D(d_ff_1_q), .clk(STCP), .Q(d_ff_2_q));  // open: Qn, preset, reset
  D_Flip_Flop d_ff_3 (.D(d_ff_1_q), .clk(SHCP), .Q(d_ff_3_q), .reset(not_1_out));  // open: Qn, preset
  assign Q0 = not_2_out ? d_ff_2_q : 1'bz;  // Controlled_Buffer controlled_buffer_1
  D_Flip_Flop d_ff_4 (.D(d_ff_3_q), .clk(SHCP), .Q(d_ff_4_q), .reset(not_1_out));  // open: Qn, preset
  D_Flip_Flop d_ff_5 (.D(d_ff_3_q), .clk(STCP), .Q(d_ff_5_q));  // open: Qn, preset, reset
  D_Flip_Flop d_ff_6 (.D(d_ff_4_q), .clk(STCP), .Q(d_ff_6_q));  // open: Qn, preset, reset
  assign Q1 = not_2_out ? d_ff_5_q : 1'bz;  // Controlled_Buffer controlled_buffer_2
  D_Flip_Flop d_ff_7 (.D(d_ff_4_q), .clk(SHCP), .Q(d_ff_7_q), .reset(not_1_out));  // open: Qn, preset
  assign Q2 = not_2_out ? d_ff_6_q : 1'bz;  // Controlled_Buffer controlled_buffer_3
  D_Flip_Flop d_ff_8 (.D(d_ff_7_q), .clk(SHCP), .Q(d_ff_8_q), .reset(not_1_out));  // open: Qn, preset
  D_Flip_Flop d_ff_9 (.D(d_ff_7_q), .clk(STCP), .Q(d_ff_9_q));  // open: Qn, preset, reset
  D_Flip_Flop d_ff_10 (.D(d_ff_8_q), .clk(STCP), .Q(d_ff_10_q));  // open: Qn, preset, reset
  assign Q3 = not_2_out ? d_ff_9_q : 1'bz;  // Controlled_Buffer controlled_buffer_4
  D_Flip_Flop d_ff_11 (.D(d_ff_8_q), .clk(SHCP), .Q(d_ff_11_q), .reset(not_1_out));  // open: Qn, preset
  assign Q4 = not_2_out ? d_ff_10_q : 1'bz;  // Controlled_Buffer controlled_buffer_5
  D_Flip_Flop d_ff_12 (.D(d_ff_11_q), .clk(SHCP), .Q(d_ff_12_q), .reset(not_1_out));  // open: Qn, preset
  D_Flip_Flop d_ff_13 (.D(d_ff_11_q), .clk(STCP), .Q(d_ff_13_q));  // open: Qn, preset, reset
  D_Flip_Flop d_ff_14 (.D(d_ff_12_q), .clk(STCP), .Q(d_ff_14_q));  // open: Qn, preset, reset
  assign Q5 = not_2_out ? d_ff_13_q : 1'bz;  // Controlled_Buffer controlled_buffer_6
  D_Flip_Flop d_ff_15 (.D(d_ff_12_q), .clk(SHCP), .Q(Q7s), .reset(not_1_out));  // open: Qn, preset
  assign Q6 = not_2_out ? d_ff_14_q : 1'bz;  // Controlled_Buffer controlled_buffer_7
  D_Flip_Flop d_ff_16 (.D(Q7s), .clk(STCP), .Q(d_ff_16_q));  // open: Qn, preset, reset
  assign Q7 = not_2_out ? d_ff_16_q : 1'bz;  // Controlled_Buffer controlled_buffer_8
endmodule

module PISO_4BIT (
  input  D0,
  input  D1,
  input  D2,
  input  D3,
  input  LOAD_DATA,
  input  CLOCK,
  output DATA_OUT
);

  wire d_ff_1_q, d_ff_2_q, d_ff_3_q, multiplexer_1_out, multiplexer_2_out, multiplexer_3_out,
       multiplexer_4_out, not_1_out;

  not not_1 (not_1_out, LOAD_DATA);
  D_Flip_Flop d_ff_1 (.D(multiplexer_1_out), .clk(CLOCK), .Q(d_ff_1_q));  // open: Qn, preset, reset
  Multiplexer #(.enable("false")) multiplexer_1 (.in0(D0), .in1(1'b0), .out(multiplexer_1_out), .sel(not_1_out));
  Multiplexer #(.enable("false")) multiplexer_2 (.in0(D1), .in1(d_ff_1_q), .out(multiplexer_2_out), .sel(not_1_out));
  D_Flip_Flop d_ff_2 (.D(multiplexer_2_out), .clk(CLOCK), .Q(d_ff_2_q));  // open: Qn, preset, reset
  D_Flip_Flop d_ff_3 (.D(multiplexer_3_out), .clk(CLOCK), .Q(d_ff_3_q));  // open: Qn, preset, reset
  Multiplexer #(.enable("false")) multiplexer_3 (.in0(D2), .in1(d_ff_2_q), .out(multiplexer_3_out), .sel(not_1_out));
  Multiplexer #(.enable("false")) multiplexer_4 (.in0(D3), .in1(d_ff_3_q), .out(multiplexer_4_out), .sel(not_1_out));
  D_Flip_Flop d_ff_4 (.D(multiplexer_4_out), .clk(CLOCK), .Q(DATA_OUT));  // open: Qn, preset, reset
endmodule

module SIPO_4BIT (
  input  DATA_IN,
  input  CLOCK,
  output Q0,
  output Q1,
  output Q2,
  output Q3
);

  D_Flip_Flop d_ff_1 (.D(DATA_IN), .clk(CLOCK), .Q(Q0));  // open: Qn, preset, reset
  D_Flip_Flop d_ff_2 (.D(Q0), .clk(CLOCK), .Q(Q1));  // open: Qn, preset, reset
  D_Flip_Flop d_ff_3 (.D(Q1), .clk(CLOCK), .Q(Q2));  // open: Qn, preset, reset
  D_Flip_Flop d_ff_4 (.D(Q2), .clk(CLOCK), .Q(Q3));  // open: Qn, preset, reset
endmodule

module Cascade (
  input  in_1,
  input  in_2,
  input  in_3
);

  wire clock_1_out, clock_2_out, shreg74hc595_1_q0, shreg74hc595_1_q1, shreg74hc595_1_q2, shreg74hc595_1_q3,
       shreg74hc595_1_q4, shreg74hc595_1_q5, shreg74hc595_1_q6, shreg74hc595_1_q7, shreg74hc595_1_q7s,
       shreg74hc595_2_q0, shreg74hc595_2_q1, shreg74hc595_2_q2, shreg74hc595_2_q3, shreg74hc595_2_q4,
       shreg74hc595_2_q5, shreg74hc595_2_q6, shreg74hc595_2_q7;

  _7_Segment_Display u_7_segment_display_1 (
    .g(shreg74hc595_1_q0), .f(shreg74hc595_1_q1), .a(shreg74hc595_1_q2), .b(shreg74hc595_1_q3),
    .e(shreg74hc595_1_q7), .d(shreg74hc595_1_q6), .c(shreg74hc595_1_q5), .dp(shreg74hc595_1_q4));
  _7_Segment_Display u_7_segment_display_2 (
    .g(shreg74hc595_2_q0), .f(shreg74hc595_2_q1), .a(shreg74hc595_2_q2), .b(shreg74hc595_2_q3),
    .e(shreg74hc595_2_q7), .d(shreg74hc595_2_q6), .c(shreg74hc595_2_q5), .dp(shreg74hc595_2_q4));
  ShReg74HC595 shreg74hc595_1 (
    .Q3(shreg74hc595_1_q3), .Q1(shreg74hc595_1_q1), .Q7s(shreg74hc595_1_q7s), .STCP(clock_1_out),
    .SHCP(clock_2_out), .Q5(shreg74hc595_1_q5), .DS(in_1), .MR(in_3), .OE(in_2), .Q0(shreg74hc595_1_q0),
    .Q2(shreg74hc595_1_q2), .Q4(shreg74hc595_1_q4), .Q6(shreg74hc595_1_q6), .Q7(shreg74hc595_1_q7));
  ShReg74HC595 shreg74hc595_2 (
    .Q3(shreg74hc595_2_q3), .Q1(shreg74hc595_2_q1), .STCP(clock_1_out), .SHCP(clock_2_out),
    .Q5(shreg74hc595_2_q5), .DS(shreg74hc595_1_q7s), .MR(in_3), .OE(in_2), .Q0(shreg74hc595_2_q0),
    .Q2(shreg74hc595_2_q2), .Q4(shreg74hc595_2_q4), .Q6(shreg74hc595_2_q6), .Q7(shreg74hc595_2_q7));  // open: Q7s
  Clock #(.lowDuration(31)) clock_1 (.out(clock_1_out));
  Clock clock_2 (.out(clock_2_out));
endmodule

module SevenSegment (
  input  A,
  input  B,
  input  C,
  input  D,
  input  E,
  input  F,
  input  G,
  input  DP
);

  _7_Segment_Display u_7_segment_display_1 (.g(G), .f(F), .a(A), .b(B), .e(E), .d(D), .c(C), .dp(DP));
endmodule
